# Fritzing sketch 3xstm32-withmcp2515 (saved by Fritzing 0.9.6b)

parts:
  multiserial = BluePill
  stm32f103c6-canbus = BluePill
  stm32-slcan = BluePill

nets:
  N1: multiserial.A3, stm32-slcan.A2
  N2: multiserial.A10, stm32f103c6-canbus.A2
  N3: multiserial.A9, stm32f103c6-canbus.A3
  N4: multiserial.A2, stm32-slcan.A3
